# Fritzing sketch Voltmeter_Using_Arduino (saved by Fritzing 0.9.3b)
breadboards: 1

parts:
  Part1 = Arduino Uno (Rev3) - ICSP
  R1 = Resistor [tolerance=±5% resistance=1k package=THT]
  R2 = Resistor [tolerance=±5% resistance=10k package=THT]
  LCD2 = LCD screen
  LCM1602_IIC1 = LCM1602 IIC [part_number="LCM1602 IIC" chip_label="LCM1602 IIC" package="DIP (Dual Inline) [THT]"]

nets:
  N1: Part1.A1, R1.Pin_1, R2.Pin_1
  N2: Part1.A4/SDA, LCM1602_IIC1.SDA
  N3: Part1.A5/SCL, LCM1602_IIC1.SCL
  5V: Part1.5V, LCM1602_IIC1.VCC
  GND: Part1.GND, R2.Pin_0, LCM1602_IIC1.GND
  VSS: LCD2.VSS, LCM1602_IIC1.VSS
  VDD: LCD2.VDD, LCM1602_IIC1.VDD
  N4: LCD2.V0, LCM1602_IIC1.V0
  N5: LCD2.RS, LCM1602_IIC1.RS
  N6: LCD2.R/W, LCM1602_IIC1.RW
  N7: LCD2.E, LCM1602_IIC1.E
  N8: LCD2.DB0, LCM1602_IIC1.D0
  N9: LCD2.DB1, LCM1602_IIC1.D1
  N10: LCD2.DB2, LCM1602_IIC1.D2
  N11: LCD2.DB3, LCM1602_IIC1.D3
  N12: LCD2.DB4, LCM1602_IIC1.D4
  N13: LCD2.DB5, LCM1602_IIC1.D5
  N14: LCD2.DB6, LCM1602_IIC1.D6
  N15: LCD2.DB7, LCM1602_IIC1.D7
  N16: LCD2.LED+, LCM1602_IIC1.A
  N17: LCD2.LED-, LCM1602_IIC1.K

custom parts:
  LCM1602 IIC: I2C-Module to use a 1602 or 2004 LCD on with the wire.h libory Serial LCD Modul
